# Fritzing sketch morse (saved by Fritzing 0.9.3b)
breadboards: 1

parts:
  Transmitter = Arduino Uno (Rev3)
  Receiver = Arduino Uno (Rev3)
  J1 = Piezo Speaker

nets:
  N1: Transmitter.D9_PWM, Receiver.D9_PWM, J1.pin2
  GND: Transmitter.GND, Receiver.GND, J1.pin1
